# Fritzing sketch dht (saved by Fritzing 0.9.4)
breadboards: 1

parts:
  Part1 = LCD1602-I2C
  Part2 = KY-015 Temperature & Humidity Sensor Module [package="Breakout board"]
  Part3 = Arduino Uno (Rev3) - ICSP

nets:
  GND: Part1.GND, Part2.-, Part3.GND
  VCC: Part1.VCC, Part2.S, Part3.5V
  N1: Part1.SDA, Part3.A4/SDA
  N2: Part1.SCL, Part3.A5/SCL
  N3: Part2.Vin, Part3.D2

custom parts:
  LCD1602-I2C: A standard character display, usually with 2x16 characters. Comes in many colors with LCM1602 IIC attached.
  KY-015 Temperature & Humidity Sensor Module: KY-015 temperature and humidity sensor module, provides a low-latency serial interface to measure humidity and temperature.
